// Logisim project RiskVCPU.circ as structural Verilog: 6 circuits, main circuit RiskVCPU
module RiskVCPU (
  input  SysClk,
  input  Reset,
  input  PCWEn,
  input  [31:0] Instruction,
  output halt,
  output [31:0] OutTest
);

  wire ASel, BSel, ecall, FWD_A, FWD_B, ID_EX_ASel, ID_EX_BSel, ID_EX_ebreak, ID_EX_ecall, ID_EX_FLUSH,
       ID_EX_MemRead, ID_EX_MemWrite, ID_EX_RegWEn, ID_EX_WE, IF_ID_FLUSH, IF_ID_WE, MemRead, MemWrite,
       PC_WE, PCSel, RegWEn, SysClk_t;
  wire [1:0] AddrOffset, ID_EX_WBSel, WBSel;
  wire [2:0] ID_EX_MemByteSel, ImmSel, MemByteSel;
  wire [3:0] StoreMask;
  wire [4:0] ALUSel, BrSel, ID_EX_ALUSel, ID_EX_BrSel, ID_EX_rdi, ID_EX_rs1, rdi, rs1, rs2;
  wire [6:0] op_code;
  wire [31:0] ALUOut, bit_extender_1_out, bit_extender_2_out, ID_EX_Imm, ID_EX_PC, ID_EX_PC_4, ID_EX_RDataA,
       ID_EX_RDataB, IF_ID_Inst, IF_ID_PC, IF_ID_PC_4, ImmGenOut, Inst, MemInAligned, MemOut, MemOutAligned,
       MemWriteData, PC, PCPlus4, RDataA, RDataB, RegWBData;

  Clock clock_1 (.out(SysClk_t));
  // Probe on nothing
  // Probe on PC
  // Probe on PCPlus4
  // Probe on Inst
  ProgramCounter programcounter_1 (
    .TargetAddr(ALUOut), .BranchCtl(PCSel), .PCWEn(PC_WE), .Clk(SysClk_t), .Reset(1'b0), .PcOut(PC),
    .PcPlus4(PCPlus4));
  IMem imem_1 (.PC(PC), .Inst(Inst));
  PipelineReg32Bit ID_ID_INST (.DataIn(Inst), .WE(IF_ID_WE), .FLUSH(IF_ID_FLUSH), .clk(SysClk_t), .DataOut(IF_ID_Inst));
  PipelineReg32Bit u_IF_ID_PC (.DataIn(PC), .WE(IF_ID_WE), .clk(SysClk_t), .DataOut(IF_ID_PC));  // open: FLUSH
  PipelineReg32Bit u_IF_ID_PC_4 (.DataIn(PCPlus4), .WE(IF_ID_WE), .clk(SysClk_t), .DataOut(IF_ID_PC_4));  // open: FLUSH
  // Probe on ImmGenOut
  // Probe on RDataA
  // Probe on RDataB
  // Probe on RegWBData
  MainController maincontroller_1 (
    .Inst(IF_ID_Inst), .ImmSel(ImmSel), .ASel(ASel), .BSel(BSel), .ALUSel(ALUSel), .BrSel(BrSel),
    .MemRead(MemRead), .MemWrite(MemWrite), .MemByteSel(MemByteSel), .RegWEn(RegWEn), .WBSel(WBSel),
    .Is_Ecall(ecall), .Is_Ebreak(halt), .rdi(rdi), .rs1(rs1), .rs2(rs2), .op_code(op_code));
  ImmGen immgen_1 (.InstIn(IF_ID_Inst), .ImmSelIn(ImmSel), .ImmOut(ImmGenOut));
  RegisterFile registerfile_1 (
    .Data(RegWBData), .RdAddr(rdi), .Rs1Addr(rs1), .Rs2Addr(rs2), .WriteEnable(RegWEn), .Clk(SysClk_t),
    .Rs1Out(RDataA), .Rs2Out(RDataB));
  // HazardControl hazardcontrol_1: pin names not known; wires that end beside it: PCSel, rs1, rs2, PC_WE, IF_ID_WE, IF_ID_FLUSH, FWD_A, FWD_B, ID_EX_WE, ID_EX_FLUSH
  // Probe on ImmSel
  // Probe on ASel
  // Probe on BSel
  // Probe on ALUSel
  // Probe on BrSel
  // Probe on MemRead
  // Probe on MemWrite
  // Probe on MemByteSel
  // Probe on RegWEn
  // Probe on WBSel
  // Probe on ecall
  // Probe on halt
  // Probe on rdi
  // Probe on rs1
  // Probe on rs2
  PipelineReg32Bit u_ID_EX_RDataA (
    .DataIn(RDataA), .WE(ID_EX_WE), .FLUSH(ID_EX_FLUSH), .clk(SysClk_t), .DataOut(ID_EX_RDataA));
  PipelineReg32Bit u_ID_EX_RDataB (
    .DataIn(RDataB), .WE(ID_EX_WE), .FLUSH(ID_EX_FLUSH), .clk(SysClk_t), .DataOut(ID_EX_RDataB));
  PipelineReg32Bit u_ID_EX_Imm (
    .DataIn(ImmGenOut), .WE(ID_EX_WE), .FLUSH(ID_EX_FLUSH), .clk(SysClk_t), .DataOut(ID_EX_Imm));
  PipelineReg1Bit u_ID_EX_ASel (
    .DataIn(ASel), .WE(ID_EX_WE), .FLUSH(ID_EX_FLUSH), .clk(SysClk_t), .DataOut(ID_EX_ASel));
  PipelineReg1Bit u_ID_EX_BSel (
    .DataIn(BSel), .WE(ID_EX_WE), .FLUSH(ID_EX_FLUSH), .clk(SysClk_t), .DataOut(ID_EX_BSel));
  PipelineReg5Bit u_ID_EX_ALUSel (
    .DataIn(ALUSel), .WE(ID_EX_WE), .FLUSH(ID_EX_FLUSH), .clk(SysClk_t), .DataOut(ID_EX_ALUSel));
  PipelineReg5Bit u_ID_EX_BrSel (
    .DataIn(BrSel), .WE(ID_EX_WE), .FLUSH(ID_EX_FLUSH), .clk(SysClk_t), .DataOut(ID_EX_BrSel));
  PipelineReg1Bit u_ID_EX_MemRead (
    .DataIn(MemRead), .WE(ID_EX_WE), .FLUSH(ID_EX_FLUSH), .clk(SysClk_t), .DataOut(ID_EX_MemRead));
  PipelineReg1Bit u_ID_EX_MemWrite (
    .DataIn(MemWrite), .WE(ID_EX_WE), .FLUSH(ID_EX_FLUSH), .clk(SysClk_t), .DataOut(ID_EX_MemWrite));
  PipelineReg3Bit u_ID_EX_MemByteSel (
    .DataIn(MemByteSel), .WE(ID_EX_WE), .FLUSH(ID_EX_FLUSH), .clk(SysClk_t), .DataOut(ID_EX_MemByteSel));
  PipelineReg1Bit u_ID_EX_RegWEn (
    .DataIn(RegWEn), .WE(ID_EX_WE), .FLUSH(ID_EX_FLUSH), .clk(SysClk_t), .DataOut(ID_EX_RegWEn));
  PipelineReg2Bit u_ID_EX_WBSel (
    .DataIn(WBSel), .WE(ID_EX_WE), .FLUSH(ID_EX_FLUSH), .clk(SysClk_t), .DataOut(ID_EX_WBSel));
  PipelineReg1Bit u_ID_EX_ecall (
    .DataIn(ecall), .WE(ID_EX_WE), .FLUSH(ID_EX_FLUSH), .clk(SysClk_t), .DataOut(ID_EX_ecall));
  PipelineReg1Bit u_ID_EX_ebreak (
    .DataIn(halt), .WE(ID_EX_WE), .FLUSH(ID_EX_FLUSH), .clk(SysClk_t), .DataOut(ID_EX_ebreak));
  PipelineReg5Bit u_ID_EX_rdi (.DataIn(rdi), .WE(ID_EX_WE), .FLUSH(ID_EX_FLUSH), .clk(SysClk_t), .DataOut(ID_EX_rdi));
  PipelineReg5Bit u_ID_EX_rs1 (.DataIn(rs1), .WE(ID_EX_WE), .FLUSH(ID_EX_FLUSH), .clk(SysClk_t), .DataOut(ID_EX_rs1));
  PipelineReg5Bit ID_EX_rs2 (.DataIn(rs2), .WE(ID_EX_WE), .FLUSH(ID_EX_FLUSH), .clk(SysClk_t), .DataOut(ID_EX_rs1));
  PipelineReg32Bit u_ID_EX_PC (.DataIn(IF_ID_PC), .WE(ID_EX_WE), .clk(SysClk_t), .DataOut(ID_EX_PC));  // open: FLUSH
  PipelineReg32Bit u_ID_EX_PC_4 (
    .DataIn(IF_ID_PC_4), .WE(ID_EX_WE), .clk(SysClk_t), .DataOut(ID_EX_PC_4));  // open: FLUSH
  // Probe on PCSel
  // Probe on ALUOut
  BranchController branchcontroller_1 (.DataA(RDataA), .DataB(RDataB), .BrSel(BrSel), .TakeBranch(PCSel));
  ALUControl alucontrol_1 (
    .RDataA(RDataA), .PC(IF_ID_PC), .ASel(ASel), .RDataB(RDataB), .ImmVal(ImmGenOut), .BSel(BSel),
    .ALUSel(ALUSel), .Out0(ALUOut));
  // Probe on MemWriteData
  // Probe on RDataB
  // Probe on AddrOffset
  // Probe on MemByteSel
  // Probe on MemOut
  // Probe on MemInAligned
  // Probe on MemOutAligned
  // Probe on AddrOffset
  DMem dmem_1 (
    .AluOut(ALUOut), .MemWrite(MemWrite), .MemRead(MemRead), .StoreMast(StoreMask), .clk(SysClk_t),
    .WriteData(MemWriteData), .AddrOffset(AddrOffset), .MemOut(MemOut));
  StoreAligner storealigner_1 (
    .Data(RDataB), .AddrOffset(AddrOffset), .ByteSel(MemByteSel), .DataOut(MemWriteData), .MaskOut(StoreMask));
  LoadAligner loadaligner_1 (.AddrOffset(AddrOffset), .Data(MemOut), .ByteSel(MemByteSel), .Out0(MemOutAligned));
  // Probe on WBSel
  // Probe on RegWBData
  assign bit_extender_1_out = {{31{MemWrite}}, MemWrite};  // Bit_Extender bit_extender_1
  assign bit_extender_2_out = {{31{halt}}, halt};  // Bit_Extender bit_extender_2
  WriteBackControl writebackcontrol_1 (
    .ALUOut(ALUOut), .MemOut(MemOutAligned), .PCPlus4(IF_ID_PC_4), .WBSel(WBSel), .OutData(RegWBData));
  assign OutTest = MemWriteData & bit_extender_2_out & bit_extender_1_out;  // AND_Gate and_1, 32 bits wide

  // Other names for the same wires on the sheet: ebreak = halt

  // Notes on the sheet:
  //   IF - Instruction Fetch
  //   IF_ID
  //   ID - Instruction Decode
  //   TODO: MUX ON FWD_A
  //   TODO: MUX ON FWD_B
  //   ID_EX
  //   EX - Execute
  //   MEM - Memory
  //   00 = ALU
  //   01 = Mem
  //   11 = PCPlus4
  //   WB - Write Back
endmodule

module PipelineReg32Bit (
  input  [31:0] DataIn,
  input  WE,
  input  FLUSH,
  input  clk,
  output [31:0] DataOut
);

  wire or_1_out;
  wire [31:0] multiplexer_1_out;

  // Probe on multiplexer_1_out
  Multiplexer #(.width(32)) multiplexer_1 (.in0(DataIn), .in1({32{1'b0}}), .out(multiplexer_1_out), .sel(FLUSH));
  or or_1 (or_1_out, WE, FLUSH);
  Register #(.width(32)) register_1 (.D(multiplexer_1_out), .en(or_1_out), .clk(clk), .Q(DataOut));  // open: clr
  // Probe on DataOut

  // Other names for the same wires on the sheet: data[31:0] = DataIn
endmodule

module PipelineReg5Bit (
  input  [4:0] DataIn,
  input  WE,
  input  FLUSH,
  input  clk,
  output [4:0] DataOut
);

  wire or_1_out;
  wire [4:0] multiplexer_1_out;

  // Probe on multiplexer_1_out
  Multiplexer #(.width(5)) multiplexer_1 (.in0(DataIn), .in1({5{1'b0}}), .out(multiplexer_1_out), .sel(FLUSH));
  or or_1 (or_1_out, WE, FLUSH);
  Register #(.width(5)) register_1 (.D(multiplexer_1_out), .en(or_1_out), .clk(clk), .Q(DataOut));  // open: clr
  // Probe on DataOut

  // Other names for the same wires on the sheet: data[4:0] = DataIn
endmodule

module PipelineReg1Bit (
  input  DataIn,
  input  WE,
  input  FLUSH,
  input  clk,
  output DataOut
);

  wire multiplexer_1_out, or_1_out;

  // Probe on multiplexer_1_out
  Multiplexer multiplexer_1 (.in0(DataIn), .in1(1'b0), .out(multiplexer_1_out), .sel(FLUSH));
  or or_1 (or_1_out, WE, FLUSH);
  Register #(.width(1)) register_1 (.D(multiplexer_1_out), .en(or_1_out), .clk(clk), .Q(DataOut));  // open: clr
  // Probe on DataOut

  // Other names for the same wires on the sheet: data = DataIn
endmodule

module PipelineReg3Bit (
  input  [2:0] DataIn,
  input  WE,
  input  FLUSH,
  input  clk,
  output [2:0] DataOut
);

  wire or_1_out;
  wire [2:0] multiplexer_1_out;

  // Probe on multiplexer_1_out
  Multiplexer #(.width(3)) multiplexer_1 (.in0(DataIn), .in1(3'b000), .out(multiplexer_1_out), .sel(FLUSH));
  or or_1 (or_1_out, WE, FLUSH);
  Register #(.width(3)) register_1 (.D(multiplexer_1_out), .en(or_1_out), .clk(clk), .Q(DataOut));  // open: clr
  // Probe on DataOut

  // Other names for the same wires on the sheet: data[2:0] = DataIn
endmodule

module PipelineReg2Bit (
  input  [1:0] DataIn,
  input  WE,
  input  FLUSH,
  input  clk,
  output [1:0] DataOut
);

  wire or_1_out;
  wire [1:0] multiplexer_1_out;

  // Probe on multiplexer_1_out
  Multiplexer #(.width(2)) multiplexer_1 (.in0(DataIn), .in1(2'b00), .out(multiplexer_1_out), .sel(FLUSH));
  or or_1 (or_1_out, WE, FLUSH);
  Register #(.width(2)) register_1 (.D(multiplexer_1_out), .en(or_1_out), .clk(clk), .Q(DataOut));  // open: clr
  // Probe on DataOut

  // Other names for the same wires on the sheet: data[1:0] = DataIn
endmodule
